# Fritzing sketch 8d5a105f-6e61-46d1-a160-2962547bdaee (saved by Fritzing 0.9.3b)
breadboards: 1

parts:
  R1 = Resistor [tolerance=±5% resistance=220 package=THT]  # not connected
  Q1 = PNP-Transistor [package="TO92 [THT]"]  # not connected
  S1 = Pushbutton [package="[THT]"]

nets:
  N1: S1.Pin_1, S1.Pin_2
  N2: S1.Pin_3, S1.Pin_4
